# Fritzing sketch v1.0.1 (saved by Fritzing 0.9.4)
circuit board: 6cm x 8cm

parts:
  J63 = female pin header, 1 pin [form="♀ (female)"]  # not connected
  J124 = female pin header, 1 pin [form="♀ (female)"]  # not connected
  J183 = female pin header, 1 pin [form="♀ (female)"]  # not connected
  J4 = shrouded pin header, 40 pins [form="♂ (shrouded male)"]
  A5_A7 = female pin header, 2 pins [form="♀ (female)"]
  J3 = screw terminal, 2 pins  # not connected
  J212 = female pin header, 1 pin [form="♀ (female)"]  # not connected
  D15 = Diode [part_number=SS54 package=sma-diode]  # not connected
  Part23 = TE_Con_316370-6_040_II SRS_MK-II_48Pin_CAP-ASSY [part_number=316370-6 package="48-pin 0.040\" 3 row"]

nets:
  INJ-1-OUT: J4.pin1, J4.pin40, Part23.2V, Part23.2W, Part23.2X
  INJ-2-OUT: J4.pin2, J4.pin39, Part23.2S, Part23.2T, Part23.2U
  INJ-3-OUT: J4.pin3, J4.pin4, Part23.2P, Part23.2Q, Part23.2R
  INJ-4-OUT: J4.pin5, J4.pin6, Part23.2N, Part23.2O
  IGN-1-OUT: J4.pin7
  IGN-4-OUT: J4.pin8
  GND: J4.pin9, J4.pin10, J4.pin12, J4.pin23
  ACD Clamp 9/MAP-CPU-A3: J4.pin11
  5V: J4.pin13, J4.pin28
  ETH-ICD14: J4.pin14
  Fan-IDC15: J4.pin15
  FuelPump-IDC16: J4.pin16
  TacH-IDC17: J4.pin17
  Clutch-IDC18: J4.pin18
  CLT Sensor: J4.pin19
  IAT Sensor: J4.pin20
  O2 Sensor: J4.pin21
  TPS Sensor: J4.pin22
  VR2+: J4.pin24
  VR1+: J4.pin25
  VR2-: J4.pin26
  VR1-: J4.pin27
  STEP-2B-OUT: J4.pin29
  STEP-2A-OUT: J4.pin30
  STEP-1A-OUT: J4.pin31
  STEP-1B-OUT: J4.pin32
  IGN-3-OUT: J4.pin33
  IGN-2-OUT: J4.pin34
  BOOST-OUT: J4.pin35
  HC-1-OUT: J4.pin36
  IDLE-OUT: J4.pin37
  HC-2-OUT: J4.pin38
  A7: A5_A7.pin1
  A5: A5_A7.pin2

notes:
  Injector 1
  Injector 3
  Injector 2
  Injector 4
  Ignitor output 1
  Power supply
  DetonationEMS.com
  Generic Outputs - High Current
  inj1
  Reset Protection - Refer AVR040 Application note
  Stepper Driver
  PWM Idle / Boost
  Proto Area
  v1.2c
  Aaron S. 2020
  Protection
  Flex Input
  TPS Input
  o2 Input
  IAT Input
  Battery Ref
  Coolant Temp
  [ 0-5v Spare Input ]
  D43
  [ Spare Outputs ]
  D53
  D46
  D48

custom parts:
  Diode: Diode These are standard reverse protection diodes and small signal diodes. SMA package can handle up to about 1A. SOD-323 can handle about 200mA. What the SOD-323 package when ordering, there are some mfgs out there that are 5-pin packages.
  TE_Con_316370-6_040_II SRS_MK-II_48Pin_CAP-ASSY: TE Connectors_316370-6_040_II SRS_MK-II_48Pin_CAP-ASSY
