# Fritzing sketch v1.0.0 (saved by Fritzing 0.9.4)
circuit board: 10cm x 10cm
circuit board: 4.5cm x 10cm

parts:
  Arduino_Mega_2560 = Arduino Mega 2560 (Rev3) [part_number="Arduino Mega 2560"]
  Q1 = Basic FET N-Channel [part_number=STP62NS04Z package="TO220 [THT]"]
  Q2 = Basic FET N-Channel [part_number=STP62NS04Z package="TO220 [THT]"]
  Q3 = Basic FET N-Channel [part_number=STP62NS04Z package="TO220 [THT]"]
  Q4 = Basic FET N-Channel [part_number=STP62NS04Z package="TO220 [THT]"]
  U2 = V18ZA2P [part_number=ERZV14D220 package=v18za2p]
  IC3 = IC, DIP package, 8 pins [chip_label="Dual VR Conditioner"]
  JP1 = female pin header, 3 pins [form="♀ (female)"]
  JP2 = female pin header, 3 pins [form="♀ (female)"]
  JP3 = female pin header, 3 pins [form="♀ (female)"]
  JP4 = female pin header, 2 pins [form="♀ (female)"]
  JP5 = female pin header, 2 pins [form="♀ (female)"]
  Q5 = Basic FET N-Channel [part_number=STP62NS04Z package="TO220 [THT]"]
  Q7 = Basic FET N-Channel [part_number=STP62NS04Z package="TO220 [THT]"]
  Q6 = Basic FET N-Channel [part_number=STP62NS04Z package="TO220 [THT]"]
  Q8 = Basic FET N-Channel [part_number=STP62NS04Z package="TO220 [THT]"]
  J143 = female pin header, 1 pin [form="♀ (female)"]  # not connected
  J144 = female pin header, 1 pin [form="♀ (female)"]  # not connected
  C5 = Ceramic Capacitor [capacitance=0.1µF package="0805 [SMD, multilayer]"]
  C20 = Ceramic Capacitor [capacitance=1µF package="0805 [SMD, multilayer]"]
  C12 = Ceramic Capacitor [capacitance=1µF package="0805 [SMD, multilayer]"]
  C4 = Ceramic Capacitor [capacitance=0.22µF package="0805 [SMD, multilayer]"]
  R62 = Resistor [tolerance=±5% resistance=120 package="0805 [SMD]"]
  C2 = Ceramic Capacitor [capacitance=0.22µF package="0805 [SMD, multilayer]"]
  R7 = Resistor [tolerance=±0.1% resistance=3.9k package="0805 [SMD]"]
  R1 = Resistor [tolerance=±0.1% resistance=2.49k package="0805 [SMD]"]
  C8 = Ceramic Capacitor [capacitance=0.22µF package="0805 [SMD, multilayer]"]
  C7 = Ceramic Capacitor [capacitance=0.1µF package="0805 [SMD, multilayer]"]
  R59 = Resistor [tolerance=±5% resistance=220 package="0805 [SMD]"]
  R40 = Resistor [tolerance=±5% resistance=1k package="0805 [SMD]"]
  R39 = Resistor [tolerance=±5% resistance=1k package="0805 [SMD]"]
  R60 = Resistor [tolerance=±5% resistance=1k package="0805 [SMD]"]
  C24 = Ceramic Capacitor [capacitance=100nF package="0805 [SMD, multilayer]"]
  R3 = Resistor [tolerance=±0.1% resistance=2.49k package="0805 [SMD]"]
  C10 = Ceramic Capacitor [capacitance=0.22µF package="0805 [SMD, multilayer]"]
  C9 = Ceramic Capacitor [capacitance=0.1µF package="0805 [SMD, multilayer]"]
  C25 = Ceramic Capacitor [capacitance=0.01µF package="0805 [SMD, multilayer]"]
  C3 = Ceramic Capacitor [capacitance=0.1µF package="0805 [SMD, multilayer]"]
  R2 = Resistor [tolerance=±5% resistance=470 package="0805 [SMD]"]
  R4 = Resistor [tolerance=±5% resistance=470 package="0805 [SMD]"]
  R22 = Resistor [tolerance=±5% resistance=470 package="0805 [SMD]"]
  R6 = Resistor [tolerance=±5% resistance=470 package="0805 [SMD]"]
  C6 = Ceramic Capacitor [capacitance=0.22µF package="0805 [SMD, multilayer]"]
  R31 = Resistor [tolerance=±5% resistance=10 power=1 package="0805 [SMD]"]
  R32 = Resistor [tolerance=±5% resistance=10 power=2W package="0805 [SMD]"]
  R8 = Resistor [tolerance=±5% resistance=470 package="0805 [SMD]"]
  R21 = Resistor [tolerance=±5% resistance=1k package="0805 [SMD]"]
  R49 = Resistor [tolerance=±5% resistance=100k power=0.25W package="0805 [SMD]"]
  R55 = Resistor [tolerance=±5% resistance=100k package="0805 [SMD]"]
  R48 = Resistor [tolerance=±5% resistance=100k package="0805 [SMD]"]
  R56 = Resistor [tolerance=±5% resistance=100k power=0.25W package="0805 [SMD]"]
  R51 = Resistor [tolerance=±5% resistance=1k package="0805 [SMD]"]
  R57 = Resistor [tolerance=±5% resistance=1k package="0805 [SMD]"]
  R50 = Resistor [tolerance=±5% resistance=1k package="0805 [SMD]"]
  R58 = Resistor [tolerance=±5% resistance=1k package="0805 [SMD]"]
  R27 = Resistor [tolerance=±5% resistance=10 power=2W package="0805 [SMD]"]
  R25 = Resistor [tolerance=±5% resistance=10 power=2W package="0805 [SMD]"]
  R35 = Resistor [tolerance=±5% resistance=100k package="0805 [SMD]"]
  R37 = Resistor [tolerance=±5% resistance=100k package="0805 [SMD]"]
  R23 = Resistor [tolerance=±5% resistance=1k package="0805 [SMD]"]
  R24 = Resistor [tolerance=±5% resistance=1k package="0805 [SMD]"]
  C11 = Ceramic Capacitor [capacitance=1µF package="0805 [SMD, multilayer]"]
  R38 = Resistor [tolerance=±5% resistance=100k package="0805 [SMD]"]
  R29 = Resistor [tolerance=±5% resistance=1k package="0805 [SMD]"]
  R30 = Resistor [tolerance=±5% resistance=1k package="0805 [SMD]"]
  R36 = Resistor [tolerance=±5% resistance=100k package="0805 [SMD]"]
  R9 = Resistor [tolerance=±5% resistance=100k package="0805 [SMD]"]
  R12 = Resistor [tolerance=±5% resistance=1k power=0.25W package="0805 [SMD]"]
  R10 = Resistor [tolerance=±5% resistance=100k power=0.25W package="0805 [SMD]"]
  R11 = Resistor [tolerance=±5% resistance=1k package="0805 [SMD]"]
  R13 = Resistor [tolerance=±5% resistance=100k package="0805 [SMD]"]
  R15 = Resistor [tolerance=±5% resistance=1k package="0805 [SMD]"]
  R14 = Resistor [tolerance=±5% resistance=100k package="0805 [SMD]"]
  R16 = Resistor [tolerance=±5% resistance=1k package="0805 [SMD]"]
  R41 = Resistor [tolerance=±5% resistance=470 package="0805 [SMD]"]
  C19 = Ceramic Capacitor [capacitance=0.01µF package="0805 [SMD, multilayer]"]
  R61 = Resistor [tolerance=±5% resistance=2.49k package="0805 [SMD]"]
  C15 = Ceramic Capacitor [capacitance=0.1µF voltage=50V package="0805 [SMD, multilayer]"]
  C13 = Ceramic Capacitor [capacitance=0.1µF voltage=50V package="0805 [SMD, multilayer]"]
  J169 = female pin header, 1 pin [form="♀ (female)"]  # not connected
  J170 = female pin header, 1 pin [form="♀ (female)"]  # not connected
  J172 = female pin header, 1 pin [form="♀ (female)"]  # not connected
  J173 = female pin header, 1 pin [form="♀ (female)"]  # not connected
  J174 = female pin header, 1 pin [form="♀ (female)"]  # not connected
  J176 = female pin header, 1 pin [form="♀ (female)"]  # not connected
  J177 = female pin header, 1 pin [form="♀ (female)"]  # not connected
  J180 = female pin header, 1 pin [form="♀ (female)"]  # not connected
  J182 = female pin header, 1 pin [form="♀ (female)"]  # not connected
  J186 = female pin header, 1 pin [form="♀ (female)"]  # not connected
  D16 = Schottky Diode [part_number=1N5919BG package="300 mil [THT]"]
  HC-05 = Bluetooth HC-05 Macho
  IC6 = ULN2003A [package="SO16 [SMD]"]
  R63 = Resistor [tolerance=±5% resistance=10k package="0805 [SMD]"]
  C18 = Ceramic Capacitor [capacitance=1pF part_number=47pf package="0805 [SMD, multilayer]"]
  C16 = Tantalum Capacitor [capacitance=10µF voltage=35V package="A 3216 [SMD, tantalum]"]
  J4 = shrouded pin header, 40 pins [form="♂ (shrouded male)"]
  C30 = Ceramic Capacitor [capacitance=0.22µF package="0805 [SMD, multilayer]"]
  R65 = Resistor [tolerance=±5% resistance=220 package="0805 [SMD]"]
  C29 = Ceramic Capacitor [capacitance="100 nF" package="0805 [SMD, multilayer]"]
  C28 = Ceramic Capacitor [capacitance="100 nF" package="0805 [SMD, multilayer]"]
  C27 = Ceramic Capacitor [capacitance="100 nF" package="0805 [SMD, multilayer]"]
  C26 = Ceramic Capacitor [capacitance="100 nF" package="0805 [SMD, multilayer]"]
  R64 = Resistor [tolerance=±5% resistance=220 package="0805 [SMD]"]
  J3 = screw terminal, 2 pins
  IC4 = SO16 [chip_label=SP720 package=SO]
  IC1 = SO08-EIAJ [chip_label=IC package=SO]
  IC2 = SO08-EIAJ [chip_label=IC part_number=" C44150" package=SO]
  J210 = female pin header, 1 pin [form="♀ (female)"]  # not connected
  J211 = female pin header, 1 pin [form="♀ (female)"]  # not connected
  J213 = female pin header, 1 pin [form="♀ (female)"]  # not connected
  J215 = female pin header, 1 pin [form="♀ (female)"]  # not connected
  C1 = Ceramic Capacitor [capacitance=0.1µF package="0805 [SMD, multilayer]"]
  MPX4250AP1 = MPX4250AP pressure sensor [part_number=MPX]
  JP7 = female pin header, 2 pins [form="♀ (female)"]
  D54 = Diode [package=sma-diode]
  IC5 = SO08w [chip_label=IC package=SO(w)]
  D15 = Diode [part_number=SS54 package=sma-diode]
  R75 = Resistor [tolerance=±5% resistance=1k package="0805 [SMD]"]
  R76 = Resistor [tolerance=±5% resistance=51k package="0805 [SMD]"]
  C31 = Ceramic Capacitor [capacitance=4.7µ part_number=330nf package="0805 [SMD, multilayer]"]
  R77 = Resistor [tolerance=±5% resistance=1k package="0805 [SMD]"]
  R78 = Resistor [tolerance=±5% resistance=2.2k package="0805 [SMD]"]
  DRV8825 = DRV 8825 Stepper Motor Carrier, High Current [part_number="DRV 8825"]
  C14 = Tantalum Capacitor [capacitance=47µF voltage=10V package="A 3216 [SMD, tantalum]"]
  J216 = female pin header, 1 pin [form="♀ (female)"]  # not connected
  J217 = female pin header, 1 pin [form="♀ (female)"]  # not connected
  J218 = female pin header, 1 pin [form="♀ (female)"]  # not connected
  J219 = female pin header, 1 pin [form="♀ (female)"]  # not connected
  J220 = female pin header, 1 pin [form="♀ (female)"]  # not connected
  J221 = female pin header, 1 pin [form="♀ (female)"]  # not connected
  J222 = female pin header, 1 pin [form="♀ (female)"]  # not connected
  J223 = female pin header, 1 pin [form="♀ (female)"]  # not connected
  J224 = female pin header, 1 pin [form="♀ (female)"]  # not connected
  J109 = female pin header, 5 pins [form="♀ (female)"]
  J110 = female pin header, 5 pins [form="♀ (female)"]
  U1 = Voltage Regulator - 5V [part_number=C85225 package="DPak [SMD]"]
  R66 = Resistor [tolerance=±5% resistance=2.2 power=2W package="0603 [SMD]"]
  LED1 = smd LED [color="Red (633nm)" package="0603 [SMD]"]
  R69 = Resistor [tolerance=±5% resistance=2.2 power=2W package="0603 [SMD]"]
  R68 = Resistor [tolerance=±5% resistance=2.2 power=2W package="0603 [SMD]"]
  R67 = Resistor [tolerance=±5% resistance=2.2 power=2W package="0603 [SMD]"]
  LED2 = smd LED [color="Red (633nm)" package="0603 [SMD]"]
  LED3 = smd LED [color="Red (633nm)" package="0603 [SMD]"]
  LED4 = smd LED [color="Red (633nm)" package="0603 [SMD]"]
  C32 = Ceramic Capacitor [capacitance=10µF package="0805 [SMD, multilayer]"]
  Remove_to_Prog = female pin header, 2 pins [form="♀ (female)"]
  AUX = shrouded pin header, 8 pins [form="♂ (shrouded male)"]
  12v_GND1 = screw terminal, 2 pins
  Part24 = TE_Con_316370-6_040_II SRS_MK-II_48Pin_CAP-ASSY [part_number=316370-6 package="48-pin 0.040\" 3 row"]
  AUX1 = shrouded pin header, 8 pins [form="♂ (shrouded male)"]
  J225 = shrouded pin header, 40 pins [form="♂ (shrouded male)"]

nets:
  ADC Clamp1/O2-CPU-A8: Arduino_Mega_2560.A8, C10.1, R22.Pin_1, IC4.15
  ADC Clamp6/IAT-CPU-A0: Arduino_Mega_2560.A0, C2.1, R2.Pin_1, IC4.1
  ADC Clamp2/CLT-CPU-A1: Arduino_Mega_2560.A1, C4.1, R4.Pin_1, IC4.2
  ADC Clamp3/TPS-CPU-A2: Arduino_Mega_2560.A2, R6.Pin_1, C6.1, IC4.3
  ACD Clamp 9/MAP-CPU-A3: Arduino_Mega_2560.A3, R41.Pin_0, J4.pin11, IC4.4, C31.0
  ADC Clamp4/BRV-CPU-A4: Arduino_Mega_2560.A4, C8.0, R8.Pin_1, IC4.6
  ACD Clamp 7/Analog 2-A5: Arduino_Mega_2560.A5, C27.1, R64.Pin_1, IC4.5
  ACD Clamp 8/Analog 1-A7: Arduino_Mega_2560.A7, R65.Pin_1, C29.1, IC4.7
  SCL-CPU-D21: Arduino_Mega_2560.D21/SCL
  ADC Clamp5/TACH1-CPU-D19: Arduino_Mega_2560.D19/RX1, IC3.pin8, R59.Pin_1, C25.1, IC4.10
  ADC Clamp 10/TACH2-CPU-D18: Arduino_Mega_2560.D18/TX1, IC3.pin7, R60.Pin_1, C24.0, IC4.9
  STEP-CPU-D17: Arduino_Mega_2560.D17_PWM/RX2, DRV8825.STEP
  STEPDIR-CPU-D16: Arduino_Mega_2560.D16_PWM/TX2, DRV8825.DIRECTION
  SDA-CPU-D20: Arduino_Mega_2560.SDA
  GND: Arduino_Mega_2560.GND, Q1.source, Q2.source, Q3.source, Q4.source, U2.P$2, IC3.pin6, Q5.source, Q7.source, Q6.source, Q8.source, C5.0, C20.1, C12.0, C4.0, C2.0, C8.1, C7.0, C24.1, C10.0, C9.0, C25.0, C3.0, C6.0, R21.Pin_1, R49.Pin_0, R55.Pin_0, R48.Pin_0, R56.Pin_0, R35.Pin_0, R37.Pin_0, C11.0, R38.Pin_0, R36.Pin_0, R9.Pin_1, R10.Pin_1, R13.Pin_1, R14.Pin_1, C19.1, C15.0, C13.0, D16.anode, HC-05.GND, IC6.0V, C18.1, C16.-, J4.pin9, J4.pin10, J4.pin12, J4.pin23, C30.0, C29.0, C28.0, C27.0, C26.0, J3.pin1, IC4.8, IC1.3, IC2.3, C1.0, MPX4250AP1.GND, IC5.3, R76.Pin_1, C31.1, R78.Pin_1, DRV8825.GROUND_ST/_MT, DRV8825.GROUND_LOG, C14.-, J110.pin1, J110.pin2, J110.pin3, J110.pin4, J110.pin5, U1.GND, LED1.cathode, LED2.cathode, LED3.cathode, LED4.cathode, C32.0
  INJ4-CPU-D11: Arduino_Mega_2560.D11_PWM, R14.Pin_0, R16.Pin_0
  INJ3-CPU-D10: Arduino_Mega_2560.D10_PWM, R13.Pin_0, R15.Pin_0
  INJ2-CPU-D9: Arduino_Mega_2560.D9_PWM, R12.Pin_0, R10.Pin_0
  INJ1-CPU-D8: Arduino_Mega_2560.D8_PWM, R9.Pin_0, R11.Pin_0
  RESET: Arduino_Mega_2560.RESET, Remove_to_Prog.pin2
  5V/MapPwr: Arduino_Mega_2560.5V, IC3.pin5, JP1.pin1, C20.0, R62.Pin_1, R1.Pin_0, R40.Pin_0, R39.Pin_0, R3.Pin_0, C19.0, R61.Pin_1, C13.1, D16.cathode, HC-05.VCC, J4.pin13, J4.pin28, IC4.16, MPX4250AP1.Vs, IC5.2, DRV8825.RESET, DRV8825.SLEEP, C14.+, J109.pin1, J109.pin2, J109.pin3, J109.pin4, J109.pin5, U1.output_voltage
  RX: Arduino_Mega_2560.D0_RX0, JP7.pin1, D54.A
  TX: Arduino_Mega_2560.D1_TX0, R77.Pin_1
  ADC Clamp 11/CPU-D2/ETH-ICD14: Arduino_Mega_2560.D2_PWM, R61.Pin_0, J4.pin14, C30.1, IC4.14
  CPU-D3: Arduino_Mega_2560.D3_PWM, HC-05.Key
  CPU-D4: Arduino_Mega_2560.D4_PWM, R58.Pin_0
  CPU-D5: Arduino_Mega_2560.D5_PWM, R50.Pin_0
  CPU-D6: Arduino_Mega_2560.D6_PWM, R57.Pin_0
  CPU-D7: Arduino_Mega_2560.D7_PWM, R51.Pin_0
  CPU-D24: Arduino_Mega_2560.D24, DRV8825.ENABLE
  IGN2-CPU-D24: Arduino_Mega_2560.D38, R24.Pin_0
  IGN1-CPU-D28: Arduino_Mega_2560.D40, R23.Pin_0
  LC-CPU-D43: Arduino_Mega_2560.D43, IC6.In_2
  LC-CPU-D45: Arduino_Mega_2560.D45, IC6.In_4
  LC-CPU-D46: Arduino_Mega_2560.D46, IC6.In_6
  LC-CPU-D47: Arduino_Mega_2560.D47, IC6.In_1
  LC-CPU-D48: Arduino_Mega_2560.D48, IC6.In_7
  LC-CPU-D49: Arduino_Mega_2560.D49, IC6.In_3
  IGN4-CPU-D36: Arduino_Mega_2560.D50, R30.Pin_0
  ADC Clamp 12/LC-CPU-D51: Arduino_Mega_2560.D51, IC4.11, R75.Pin_1
  IGN3-CPU-D40: Arduino_Mega_2560.D52, R29.Pin_0
  LC-CPU-D53: Arduino_Mega_2560.D53, IC6.In_5
  N1: Q1.gate, R11.Pin_1
  INJ-1-OUT: Q1.drain, J4.pin1, J4.pin40
  N2: Q2.gate, R15.Pin_1
  INJ-3-OUT: Q2.drain, J4.pin3, J4.pin4
  N3: Q3.gate, R12.Pin_1
  INJ-2-OUT: Q3.drain, J4.pin2, J4.pin39
  N4: Q4.gate, R16.Pin_1
  INJ-4-OUT: Q4.drain, J4.pin5, J4.pin6
  12V-raw: U2.P$1, JP1.pin3, R7.Pin_0, IC6.COM_-_Common, R63.Pin_1, J3.pin2, D15.A, DRV8825.VOLTAGE_ST/_MT
  VR1-: IC3.pin1, J4.pin27
  N5: IC3.pin2, JP2.pin3
  N6: IC3.pin3, JP3.pin1
  VR2-: IC3.pin4, J4.pin26
  JP1-OUT: JP1.pin2, C12.1, C11.1, IC1.6, IC2.6
  N7: JP2.pin1, R59.Pin_0
  VR1+: JP2.pin2, JP4.pin2, J4.pin25
  VR2+: JP3.pin2, JP5.pin1, J4.pin24
  N8: JP3.pin3, R60.Pin_0
  N9: JP4.pin1, R39.Pin_1
  N10: JP5.pin2, R40.Pin_1
  N11: Q5.gate, R55.Pin_1, R57.Pin_1
  HC-1-OUT: Q5.drain, J4.pin36
  N12: Q7.gate, R48.Pin_1, R50.Pin_1
  IDLE-OUT: Q7.drain, J4.pin37
  N13: Q6.gate, R56.Pin_1, R58.Pin_1
  HC-2-OUT: Q6.drain, J4.pin38
  N14: Q8.gate, R49.Pin_1, R51.Pin_1
  BOOST-OUT: Q8.drain, J4.pin35
  TPS Sensor: C5.1, R6.Pin_0, J4.pin22
  N15: R62.Pin_0, C32.1, Remove_to_Prog.pin1
  N16: R7.Pin_1, C7.1, R8.Pin_0, R21.Pin_0
  IAT Sensor: R1.Pin_1, R2.Pin_0, J4.pin20, C1.1
  CLT Sensor: R3.Pin_1, C3.1, R4.Pin_0, J4.pin19
  O2 Sensor: C9.1, R22.Pin_0, J4.pin21
  IGN-3-OUT: R31.Pin_0, J4.pin33, R69.Pin_1
  N17: R31.Pin_1, IC2.7
  N18: R32.Pin_0, IC2.5
  IGN-4-OUT: R32.Pin_1, J4.pin8, R68.Pin_1
  IGN-1-OUT: R27.Pin_0, J4.pin7, R67.Pin_1
  N19: R27.Pin_1, IC1.7
  N20: R25.Pin_0, IC1.5
  IGN-2-OUT: R25.Pin_1, J4.pin34, R66.Pin_1
  N21: R35.Pin_1, R24.Pin_1, IC1.4
  N22: R37.Pin_1, R23.Pin_1, IC1.2
  N23: R38.Pin_1, R29.Pin_1, IC2.2
  N24: R30.Pin_1, R36.Pin_1, IC2.4
  MapToECU: R41.Pin_1, C18.0, MPX4250AP1.V_out, IC5.4, R76.Pin_0
  12V: C15.1, C16.+, D15.C, U1.input_voltage
  N25: HC-05.TXD, JP7.pin2, D54.C
  N26: HC-05.RXD, R77.Pin_0, R78.Pin_0
  D48: IC6.Out_7, AUX.pin4
  D46: IC6.Out_6, AUX.pin3
  D53: IC6.Out_5, AUX.pin2
  FuelPump-IDC16: IC6.Out_4, J4.pin16
  TacH-IDC17: IC6.Out_3, R63.Pin_0, J4.pin17
  D43: IC6.Out_2, AUX.pin1
  Fan-IDC15: IC6.Out_1, J4.pin15
  Clutch-IDC18: J4.pin18, R75.Pin_0
  STEP-2B-OUT: J4.pin29, DRV8825.OUT_2B
  STEP-2A-OUT: J4.pin30, DRV8825.OUT_2A
  STEP-1A-OUT: J4.pin31, DRV8825.OUT_1A
  STEP-1B-OUT: J4.pin32, DRV8825.OUT_1B
  A7: R65.Pin_0, C28.1, AUX.pin5
  A5: C26.1, R64.Pin_0, AUX.pin6
  N27: R66.Pin_0, LED1.anode
  N28: R69.Pin_0, LED4.anode
  N29: R68.Pin_0, LED3.anode
  N30: R67.Pin_0, LED2.anode
  N31: 12v_GND1.pin2, Part24.2B
  N32: Part24.1A, AUX1.pin4
  N33: Part24.1B, AUX1.pin5
  N34: Part24.1C, AUX1.pin6
  N35: Part24.1D, AUX1.pin3
  N36: Part24.1E, Part24.1F, Part24.1H, Part24.1I, J225.pin13, J225.pin28
  N37: Part24.1G, AUX1.pin2
  N38: Part24.1J, AUX1.pin1
  N39: Part24.1L, J225.pin26
  N40: Part24.1M, J225.pin27
  N41: Part24.1N, J225.pin25
  N42: Part24.1O, J225.pin24
  N43: Part24.1P, J225.pin19
  N44: Part24.1Q, J225.pin20
  N45: Part24.1R, J225.pin22
  N46: Part24.1S, J225.pin17
  N47: Part24.1T, J225.pin18
  N48: Part24.1U, J225.pin21
  N49: Part24.1V, J225.pin15
  N50: Part24.1W, J225.pin16
  N51: Part24.1X, J225.pin14
  N52: Part24.2A, Part24.2D, Part24.2E, Part24.2G, Part24.2H
  N53: Part24.2C, J225.pin29
  N54: Part24.2F, J225.pin30
  N55: Part24.2I, J225.pin31
  N56: Part24.2J, J225.pin11
  N57: Part24.2K, J225.pin32
  N58: Part24.2L, J225.pin7
  N59: Part24.2M, J225.pin33
  N60: Part24.2N, J225.pin34
  N61: Part24.2O, J225.pin8
  N62: Part24.2P, J225.pin38
  N63: Part24.2Q, J225.pin35
  N64: Part24.2R, J225.pin36
  N65: Part24.2S, J225.pin5, J225.pin6
  N66: Part24.2U, J225.pin37
  N67: Part24.2V, J225.pin3, J225.pin4
  N68: Part24.2W, J225.pin2, J225.pin39
  N69: Part24.2X, J225.pin1, J225.pin40

notes:
  Injector 1
  Injector 3
  Injector 2
  Injector 4
  Ignitor output 1
  12v
  5v
  Power supply
  IGN Out
  DetonationEMS.com
  Generic Outputs - High Current
  inj1
  VR
  Hall
  Reset Protection - Refer AVR040 Application note
  Stepper Driver
  PWM Idle / Boost
  GND
  Proto Area
  Run  Prog
  v1.2c
  Aaron S. 2020
  Protection
  TX RX
  GND VCC
  Flex Input
  TPS Input
  o2 Input
  IAT Input
  Battery Ref
  Coolant Temp
  [ 0-5v Spare Input ]
  Select Board Layout "Speeduino V0.4"
  D43
  [ Spare Outputs ]
  D53
  D46
  D48
  Flat side down
  THT Map Sensor
  1
  4
  5
  8
  A5 A7
  GND GND
  DetonationEMS 1.3x
  DetonationEMS 1.x / Speeduino v0.4x Compatible

custom parts:
  Diode: Diode These are standard reverse protection diodes and small signal diodes. SMA package can handle up to about 1A. SOD-323 can handle about 200mA. What the SOD-323 package when ordering, there are some mfgs out there that are 5-pin packages.
  TE_Con_316370-6_040_II SRS_MK-II_48Pin_CAP-ASSY: TE Connectors_316370-6_040_II SRS_MK-II_48Pin_CAP-ASSY
