# Fritzing sketch DetonationEMS Sim (saved by Fritzing 0.9.4)
circuit board: 8.46667cm x 8cm
breadboards: 1

parts:
  Part2 = Arduino Nano (Rev3.0) (ICSP)  # not connected
  J6 = shrouded pin header, 40 pins [form="♂ (shrouded male)"]
  R8 = Resistor [tolerance=±5% resistance=330 package="0805 [SMD]"]
  R7 = Resistor [tolerance=±5% resistance=330 package="0805 [SMD]"]
  R6 = Resistor [tolerance=±5% resistance=330 package="0805 [SMD]"]
  R5 = Resistor [tolerance=±5% resistance=330 package="0805 [SMD]"]
  R1 = Resistor [tolerance=±5% resistance=330 package="0805 [SMD]"]
  R2 = Resistor [tolerance=±5% resistance=330 package="0805 [SMD]"]
  R3 = Resistor [tolerance=±5% resistance=330 package="0805 [SMD]"]
  R4 = Resistor [tolerance=±5% resistance=330 package="0805 [SMD]"]
  LED4 = smd LED [color="Red (633nm)" package="0805 [SMD]"]
  LED3 = smd LED [color="Red (633nm)" package="0805 [SMD]"]
  LED1 = smd LED [color="Red (633nm)" package="0805 [SMD]"]
  LED2 = smd LED [color="Red (633nm)" package="0805 [SMD]"]
  LED9 = smd LED [color="Red (633nm)" package="0805 [SMD]"]
  LED8 = smd LED [color="Red (633nm)" package="0805 [SMD]"]
  LED6 = smd LED [color="Red (633nm)" package="0805 [SMD]"]
  LED7 = smd LED [color="Red (633nm)" package="0805 [SMD]"]
  U1 = POT [package=alps_pot]  # not connected

nets:
  INJ-1-OUT: J6.pin1, J6.pin40, LED6.cathode
  INJ-2-OUT: J6.pin2, J6.pin39, LED7.cathode
  INJ-3-OUT: J6.pin3, J6.pin4, LED8.cathode
  INJ-4-OUT: J6.pin5, J6.pin6, LED9.cathode
  IGN-1-OUT: J6.pin7, LED1.anode
  IGN-4-OUT: J6.pin8, LED4.anode
  GND: J6.pin9, J6.pin10, J6.pin12, R1.Pin_1, R2.Pin_1, R3.Pin_1, R4.Pin_1
  MAP-CPU-A3: J6.pin11
  5V: J6.pin13, J6.pin28
  ETH-ICD14: J6.pin14
  Fan-IDC15: J6.pin15
  FuelPump-IDC16: J6.pin16
  TacH-IDC17: J6.pin17
  Clutch-IDC18: J6.pin18
  IAT Sensor: J6.pin20
  TPS Sensor: J6.pin22
  VR2+: J6.pin24
  VR1+: J6.pin25
  VR2-: J6.pin26
  VR1-: J6.pin27
  STEP-2B-OUT: J6.pin29
  STEP-2A-OUT: J6.pin30
  STEP-1A-OUT: J6.pin31
  STEP-1B-OUT: J6.pin32
  IGN-3-OUT: J6.pin33, LED3.anode
  IGN-2-OUT: J6.pin34, LED2.anode
  BOOST-OUT: J6.pin35
  HC-1-OUT: J6.pin36
  IDLE-OUT: J6.pin37
  HC-2-OUT: J6.pin38
  N1: R8.Pin_0, LED9.anode
  5v: R8.Pin_1, R7.Pin_1, R6.Pin_1, R5.Pin_1
  N2: R7.Pin_0, LED8.anode
  N3: R6.Pin_0, LED7.anode
  N4: R5.Pin_0, LED6.anode
  N5: R1.Pin_0, LED1.cathode
  N6: R2.Pin_0, LED2.cathode
  N7: R3.Pin_0, LED3.cathode
  N8: R4.Pin_0, LED4.cathode
