# Fritzing sketch v1.0.5 (saved by Fritzing 0.9.4)
circuit board: 10cm x 10cm

parts:
  D15 = Schottky Diode [part_number=1N5818 package="300 mil [THT]"]
  U2 = V18ZA2P [part_number=ERZV14D220 package=v18za2p]
  IC3 = IC, DIP package, 8 pins [chip_label="Dual VR Conditioner"]
  JP1 = female pin header, 3 pins [form="♀ (female)"]
  JP5 = female pin header, 2 pins [form="♀ (female)"]
  DRV8825 = Pololu A4988 [package=SO16]
  J142 = female pin header, 3 pins [form="♀ (female)"]
  C5 = Ceramic Capacitor [capacitance=0.1µF package="0805 [SMD, multilayer]"]
  C20 = Ceramic Capacitor [capacitance=1µF package="0805 [SMD, multilayer]"]
  C12 = Ceramic Capacitor [capacitance=1µF package="0805 [SMD, multilayer]"]
  C4 = Ceramic Capacitor [capacitance=0.22µF package="0805 [SMD, multilayer]"]
  R62 = Resistor [tolerance=±5% resistance=120 package="0805 [SMD]"]
  C2 = Ceramic Capacitor [capacitance=0.22µF package="0805 [SMD, multilayer]"]
  C1 = Ceramic Capacitor [capacitance=0.1µF package="0805 [SMD, multilayer]"]
  R7 = Resistor [tolerance=±0.1% resistance=3.9k package="0805 [SMD]"]
  R1 = Resistor [tolerance=±0.1% resistance=2.49k package="0805 [SMD]"]
  C8 = Ceramic Capacitor [capacitance=0.22µF package="0805 [SMD, multilayer]"]
  C7 = Ceramic Capacitor [capacitance=0.1µF package="0805 [SMD, multilayer]"]
  R59 = Resistor [tolerance=±5% resistance=220 package="0805 [SMD]"]
  R40 = Resistor [tolerance=±5% resistance=1k package="0805 [SMD]"]
  R39 = Resistor [tolerance=±5% resistance=1k package="0805 [SMD]"]
  R60 = Resistor [tolerance=±5% resistance=1k package="0805 [SMD]"]
  C24 = Ceramic Capacitor [capacitance=100nF package="0805 [SMD, multilayer]"]
  R3 = Resistor [tolerance=±0.1% resistance=2.49k package="0805 [SMD]"]
  C10 = Ceramic Capacitor [capacitance=0.22µF package="0805 [SMD, multilayer]"]
  C9 = Ceramic Capacitor [capacitance=0.1µF package="0805 [SMD, multilayer]"]
  C25 = Ceramic Capacitor [capacitance=0.01µF package="0805 [SMD, multilayer]"]
  C3 = Ceramic Capacitor [capacitance=0.1µF package="0805 [SMD, multilayer]"]
  R2 = Resistor [tolerance=±5% resistance=470 package="0805 [SMD]"]
  R4 = Resistor [tolerance=±5% resistance=470 package="0805 [SMD]"]
  R54 = Resistor [tolerance=±5% resistance=10k package="0805 [SMD]"]
  R22 = Resistor [tolerance=±5% resistance=470 package="0805 [SMD]"]
  R6 = Resistor [tolerance=±5% resistance=470 package="0805 [SMD]"]
  C6 = Ceramic Capacitor [capacitance=0.22µF package="0805 [SMD, multilayer]"]
  R31 = Resistor [tolerance=±5% resistance=10 power=1 package="0805 [SMD]"]
  R32 = Resistor [tolerance=±5% resistance=10 power=2W package="0805 [SMD]"]
  R8 = Resistor [tolerance=±5% resistance=470 package="0805 [SMD]"]
  R21 = Resistor [tolerance=±5% resistance=1k package="0805 [SMD]"]
  R49 = Resistor [tolerance=±5% resistance=100k power=0.25W package="0805 [SMD]"]
  R55 = Resistor [tolerance=±5% resistance=100k package="0805 [SMD]"]
  R48 = Resistor [tolerance=±5% resistance=100k package="0805 [SMD]"]
  R56 = Resistor [tolerance=±5% resistance=100k power=0.25W package="0805 [SMD]"]
  R51 = Resistor [tolerance=±5% resistance=1k package="0805 [SMD]"]
  R57 = Resistor [tolerance=±5% resistance=1k package="0805 [SMD]"]
  R50 = Resistor [tolerance=±5% resistance=1k package="0805 [SMD]"]
  R58 = Resistor [tolerance=±5% resistance=1k package="0805 [SMD]"]
  R27 = Resistor [tolerance=±5% resistance=10 power=2W package="0805 [SMD]"]
  R25 = Resistor [tolerance=±5% resistance=10 power=2W package="0805 [SMD]"]
  R35 = Resistor [tolerance=±5% resistance=100k package="0805 [SMD]"]
  R37 = Resistor [tolerance=±5% resistance=100k package="0805 [SMD]"]
  R23 = Resistor [tolerance=±5% resistance=1k package="0805 [SMD]"]
  R24 = Resistor [tolerance=±5% resistance=1k package="0805 [SMD]"]
  C11 = Ceramic Capacitor [capacitance=1µF package="0805 [SMD, multilayer]"]
  R38 = Resistor [tolerance=±5% resistance=100k package="0805 [SMD]"]
  R29 = Resistor [tolerance=±5% resistance=1k package="0805 [SMD]"]
  R30 = Resistor [tolerance=±5% resistance=1k package="0805 [SMD]"]
  R36 = Resistor [tolerance=±5% resistance=100k package="0805 [SMD]"]
  R9 = Resistor [tolerance=±5% resistance=100k package="0805 [SMD]"]
  R12 = Resistor [tolerance=±5% resistance=1k power=0.25W package="0805 [SMD]"]
  R10 = Resistor [tolerance=±5% resistance=100k power=0.25W package="0805 [SMD]"]
  R11 = Resistor [tolerance=±5% resistance=1k package="0805 [SMD]"]
  R13 = Resistor [tolerance=±5% resistance=100k package="0805 [SMD]"]
  R15 = Resistor [tolerance=±5% resistance=1k package="0805 [SMD]"]
  R14 = Resistor [tolerance=±5% resistance=100k package="0805 [SMD]"]
  R16 = Resistor [tolerance=±5% resistance=1k package="0805 [SMD]"]
  R41 = Resistor [tolerance=±5% resistance=470 package="0805 [SMD]"]
  C19 = Ceramic Capacitor [capacitance=0.01µF package="0805 [SMD, multilayer]"]
  R61 = Resistor [tolerance=±5% resistance=2.49k package="0805 [SMD]"]
  C15 = Ceramic Capacitor [capacitance=0.1µF voltage=50V package="0805 [SMD, multilayer]"]
  C13 = Ceramic Capacitor [capacitance=0.1µF voltage=50V package="0805 [SMD, multilayer]"]
  D16 = Schottky Diode [part_number=1N5818 package="300 mil [THT]"]
  R63 = Resistor [tolerance=±5% resistance=10k package="0805 [SMD]"]
  C26 = Ceramic Capacitor [capacitance=0.1µF package="0805 [SMD, multilayer]"]
  R64 = Resistor [tolerance=±5% resistance=470 package="0805 [SMD]"]
  C27 = Ceramic Capacitor [capacitance=0.22µF package="0805 [SMD, multilayer]"]
  C28 = Ceramic Capacitor [capacitance=0.1µF package="0805 [SMD, multilayer]"]
  R65 = Resistor [tolerance=±5% resistance=470 package="0805 [SMD]"]
  C29 = Ceramic Capacitor [capacitance=0.22µF package="0805 [SMD, multilayer]"]
  C23 = Ceramic Capacitor [capacitance=22µF package="0805 [SMD, multilayer]"]
  U4 = RS485 [package=so08]
  316370-6 = TE_Con_316370-6_040_II SRS_MK-II_48Pin_CAP-ASSY [part_number=316370-6 package="48-pin 0.040\" 3 row"]  # not connected
  C18 = Ceramic Capacitor [capacitance=10pF package="0805 [SMD, multilayer]"]
  IC6 = ULN2003A [package="SO16 [SMD]"]
  C14 = Tantalum Capacitor [capacitance=47µF voltage=10V package="200 mil [THT, tantalum]"]
  JP4 = female pin header, 2 pins [form="♀ (female)"]
  C16 = Tantalum Capacitor [capacitance=10µF voltage=35V package="A 3216 [SMD, tantalum]"]
  C30 = Ceramic Capacitor [capacitance=0.22µF package="0805 [SMD, multilayer]"]
  IC2 = SO08-EIAJ [chip_label=IC package=SO]
  IC1 = SO08-EIAJ [chip_label=IC package=SO]
  IC4 = SO16 [chip_label=SP720 package=SO]  # not connected
  M1 = Mega2560 R3 Pro ch340g
  U1 = Voltage Regulator - 5V [package="DPak [SMD]"]
  IC7 = SO08-EIAJ [chip_label=IC part_number=VNLD5090TR-E package=SO]
  IC8 = SO08-EIAJ [chip_label=IC part_number=VNLD5090TR-E package=SO]
  IC9 = SO08-EIAJ [chip_label=IC part_number=VNLD5090TR-E package=SO]
  IC10 = SO08-EIAJ [chip_label=IC part_number=VNLD5090TR-E package=SO]
  CMP_(JP3) = female pin header, 3 pins [form="♀ (female)"]
  CKP_(JP2) = female pin header, 3 pins [form="♀ (female)"]
  J143 = shrouded pin header, 40 pins [form="♂ (shrouded male)"]
  J144 = Screw terminal - 2 pins [package=THT]

nets:
  N1: D15.cathode, U1.input_voltage
  12V/12V-raw: D15.anode, U2.P$1, JP1.pin1, R7.Pin_0, C15.1, R63.Pin_1, IC6.COM_-_Common, C16.+, J144.pin1
  GND: U2.P$2, IC3.pin6, DRV8825.GND, C5.0, C20.0, C12.0, C4.0, C2.0, C1.0, C8.1, C7.0, C24.1, C10.0, C9.0, C25.0, C3.0, C6.0, R21.Pin_1, R49.Pin_0, R55.Pin_0, R48.Pin_0, R56.Pin_0, R35.Pin_0, R37.Pin_0, C11.0, R38.Pin_0, R36.Pin_0, R9.Pin_0, R10.Pin_0, R13.Pin_1, R14.Pin_1, C19.0, C15.0, C13.0, D16.cathode, C26.0, C27.0, C28.0, C29.0, C23.1, U4.DE, C18.1, IC6.0V, C14.-, C16.-, C30.0, IC2.3, IC1.3, M1.GND, U1.GND, IC7.5, IC7.7, IC8.5, IC8.7, IC9.5, IC9.7, IC10.5, IC10.7, J144.pin2
  VR1-: IC3.pin1
  N2: IC3.pin2, CKP_(JP2).pin3
  N3: IC3.pin3, CMP_(JP3).pin3
  VR2-: IC3.pin4
  5V: IC3.pin5, JP1.pin3, DRV8825.RESET, DRV8825.SLEEP, C20.1, R62.Pin_1, R1.Pin_0, R40.Pin_0, R39.Pin_0, R3.Pin_0, R54.Pin_1, C19.1, R61.Pin_1, C13.1, D16.anode, U4._RE, C14.+, M1.VTG, M1.5V, U1.output_voltage
  ADC Clamp7/TACH2-CPU-D18: IC3.pin7, R60.Pin_1, C24.0, M1.18
  ADC Clamp5/TACH1-CPU-D19: IC3.pin8, R59.Pin_1, C25.1, M1.19
  JP1-OUT: JP1.pin2, C12.1, C11.1, IC2.6, IC1.6
  VR2+: JP5.pin1, CMP_(JP3).pin2
  N4: JP5.pin2, R40.Pin_1
  CPU-D24: DRV8825.ENABLE
  STEP-CPU-D17: DRV8825.STEP, M1.17
  STEPDIR-CPU-D16: DRV8825.DIR, M1.16
  STEP-1B-OUT: DRV8825.1B
  STEP-1A-OUT: DRV8825.1A
  STEP-2A-OUT: DRV8825.2A
  STEP-2B-OUT: DRV8825.2B
  N5: J142.pin1, R54.Pin_0
  RESET: J142.pin2
  N6: J142.pin3, R62.Pin_0, C23.0
  TPS Sensor: C5.1, R6.Pin_0
  ADC Clamp2/CLT-CPU-A1: C4.1, R4.Pin_1, M1.A1
  ADC Clamp6/IAT-CPU-A0: C2.1, R2.Pin_1, M1.A0
  IAT Sensor: C1.1, R1.Pin_1, R2.Pin_0
  N7: R7.Pin_1, C7.1, R8.Pin_0, R21.Pin_0
  ADC Clamp4/BRV-CPU-A4: C8.0, R8.Pin_1, M1.A4
  N8: R59.Pin_0, CKP_(JP2).pin1
  N9: R39.Pin_1, JP4.pin1
  N10: R60.Pin_0, CMP_(JP3).pin1
  CLT Sensor: R3.Pin_1, C3.1, R4.Pin_0
  ADC Clamp1/O2-CPU-A8: C10.1, R22.Pin_1, M1.A8
  O2 Sensor: C9.1, R22.Pin_0
  ADC Clamp3/TPS-CPU-A2: R6.Pin_1, C6.1, M1.A2
  IGN-3-OUT: R31.Pin_0
  N11: R31.Pin_1, IC2.7
  N12: R32.Pin_0, IC2.5
  IGN-4-OUT: R32.Pin_1
  N13: R49.Pin_1, R51.Pin_1, IC10.3
  N14: R55.Pin_1, R57.Pin_1, IC9.1
  N15: R48.Pin_1, R50.Pin_1, IC10.1
  N16: R56.Pin_1, R58.Pin_1, IC9.3
  CPU-D7: R51.Pin_0, M1.7▀
  CPU-D6: R57.Pin_0, M1.6▀
  CPU-D5: R50.Pin_0, M1.5▀
  CPU-D4: R58.Pin_0, M1.4▀
  IGN-1-OUT: R27.Pin_0
  N17: R27.Pin_1, IC1.7
  N18: R25.Pin_0, IC1.5
  IGN-2-OUT: R25.Pin_1
  N19: R35.Pin_1, R24.Pin_1, IC1.4
  N20: R37.Pin_1, R23.Pin_1, IC1.2
  IGN1-CPU-D28: R23.Pin_0, M1.28
  IGN2-CPU-D24: R24.Pin_0, M1.24
  N21: R38.Pin_1, R29.Pin_1, IC2.2
  IGN3-CPU-D40: R29.Pin_0, M1.40
  IGN4-CPU-D36: R30.Pin_0, M1.36
  N22: R30.Pin_1, R36.Pin_1, IC2.4
  INJ1-CPU-D8: R9.Pin_1, R11.Pin_0, M1.8▀
  INJ2-CPU-D9: R12.Pin_0, R10.Pin_1, M1.9▀
  N23: R12.Pin_1, IC8.1
  N24: R11.Pin_1, IC7.1
  INJ3-CPU-D10: R13.Pin_0, R15.Pin_0, M1.10▀
  N25: R15.Pin_1, IC8.3
  INJ4-CPU-D11: R14.Pin_0, R16.Pin_0, M1.11▀
  N26: R16.Pin_1, IC7.3
  EXT-MAP: R41.Pin_0, U4.DI
  ACD Clamp8/MAP-CPU-A3: R41.Pin_1, C18.0, M1.A3
  ACD Clamp9/CPU-D2/Flex: R61.Pin_0, C30.1, M1.3▀
  LC-4-OUT: R63.Pin_0, IC6.Out_5
  FuelPress: C26.1, R64.Pin_0
  FuelPress-A5: R64.Pin_1, C27.1, M1.A5
  OilPress: C28.1, R65.Pin_0
  OilPress-A7: R65.Pin_1, C29.1, M1.A7
  RST-CPU-D48: IC6.In_2, M1.48
  LC-CPU-D47: IC6.In_3, M1.47
  LC-CPU-D45: IC6.In_4, M1.45
  LC-CPU-D49: IC6.In_5, M1.49
  LC-3-OUT: IC6.Out_4
  LC-2-OUT: IC6.Out_3
  LC-1-OUT: IC6.Out_2
  VR1+: JP4.pin2, CKP_(JP2).pin2
  SCL-CPU-D21: M1.21
  SDA-CPU-D20: M1.20
  LC-5-OUT/LC-CPU-D51: M1.51/MOSI
  INJ-4-OUT: IC7.6, J143.pin1, J143.pin40
  INJ-1-OUT: IC7.8, J143.pin2, J143.pin39
  INJ-3-OUT: IC8.6, J143.pin3, J143.pin38
  INJ-2-OUT: IC8.8, J143.pin4, J143.pin37
  HC-2-OUT: IC9.6, J143.pin34
  HC-1-OUT: IC9.8, J143.pin33
  BOOST-OUT: IC10.6, J143.pin36
  IDLE-OUT: IC10.8, J143.pin35

notes:
  Inlet Air Temperature sensor
  Coolant Temperature Sensor
  Speeduino v0.4, Throttle Position Sensor
  Battery Reference Voltage
  Speeduino v0.4, O2 Sensor
  Ignitor output 1
  12v
  5v
  Power supply
  IGN Out
  Crank and Cam sensors
  Speeduino v0.4, MAP sensor input
  DetonationEMS.com
  Generic Outputs - High Current
  inj1
  VR
  Hall
  Reset Protection - Refer AVR040 Application note
  Stepper Driver
  PWM Idle / Boost
  Proto Area
  Run  Prog
  Aaron S. 2020
  Flex-Fuel  Input
  ULN2003a
  PreIgnition v0.1

custom parts:
  TE_Con_316370-6_040_II SRS_MK-II_48Pin_CAP-ASSY: TE Connectors_316370-6_040_II SRS_MK-II_48Pin_CAP-ASSY
  Mega2560 R3 Pro ch340g: The Mega 2560 R3 Pro Mini :- Completely compatible with original Arduino Mega2560 Pin pitch: 0.1 inch Size: 5.42cm*3.68cm With Atmega16U2 chip as the USB to Serial converter 5V working voltage. Input Voltage:7-12V Analog Input Pins: 16 Digital I/O pins: 54 The Mega 2560 R3 Pro Mini has no datasheet and no info and I don't have one to compare, so I made this based on photos. Dec 2019 modified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
