# Fritzing sketch v0.0.7 (saved by Fritzing 0.9.4)
circuit board: 6cm x 8cm

parts:
  J4 = shrouded pin header, 40 pins [form="♂ (shrouded male)"]
  AUX = shrouded pin header, 8 pins [form="♂ (shrouded male)"]  # not connected
  Part23 = TE_Con_316370-6_040_II SRS_MK-II_48Pin_CAP-ASSY [part_number=316370-6 package="48-pin 0.040\" 3 row"]
  J5 = Screw terminal - 2 pins [package=THT]

nets:
  INJ-1-OUT: J4.pin1, J4.pin40, Part23.2X
  INJ-2-OUT: J4.pin2, J4.pin39, Part23.2W
  INJ-3-OUT: J4.pin3, J4.pin4, Part23.2V
  INJ-4-OUT: J4.pin5, J4.pin6, Part23.2S
  IGN-1-OUT: J4.pin7, Part23.2L
  IGN-4-OUT: J4.pin8, Part23.2O
  GND: J4.pin9, J4.pin10, J4.pin12, J4.pin23
  MAP-CPU-A3: J4.pin11, Part23.2J
  5V: J4.pin13, J4.pin28, Part23.1V, Part23.1W, Part23.1X
  ETH-ICD14: J4.pin14
  Fan-IDC15: J4.pin15
  FuelPump-IDC16: J4.pin16
  TacH-IDC17: J4.pin17
  Clutch-IDC18: J4.pin18
  CLT Sensor: J4.pin19
  IAT Sensor: J4.pin20
  O2 Sensor: J4.pin21, Part23.2D
  TPS Sensor: J4.pin22, Part23.2A
  VR2+: J4.pin24
  VR1+: J4.pin25
  VR2-: J4.pin26
  VR1-: J4.pin27
  STEP-2B-OUT: J4.pin29, Part23.2C
  STEP-2A-OUT: J4.pin30, Part23.2F
  STEP-1A-OUT: J4.pin31, Part23.2I
  STEP-1B-OUT: J4.pin32, Part23.2K
  IGN-3-OUT: J4.pin33, Part23.2M
  IGN-2-OUT: J4.pin34, Part23.2N
  BOOST-OUT: J4.pin35, Part23.2Q
  HC-1-OUT: J4.pin36, Part23.2R
  IDLE-OUT: J4.pin37, Part23.2U
  HC-2-OUT: J4.pin38, Part23.2P
  12V-raw: Part23.2B, J5.pin1
  N1: Part23.2E, Part23.2G, Part23.2H

notes:
  inj1
  Aaron S. 2020
  [ 0-5v Spare Input ]
  D43
  [ Spare Outputs ]
  D53
  D46
  D48
  A5 A7
  GND GND

custom parts:
  TE_Con_316370-6_040_II SRS_MK-II_48Pin_CAP-ASSY: TE Connectors_316370-6_040_II SRS_MK-II_48Pin_CAP-ASSY
