# Fritzing sketch v0.1.1 (saved by Fritzing 0.9.4)
circuit board: 10cm x 5cm

parts:
  J4 = shrouded pin header, 40 pins [form="♂ (shrouded male)"]
  AUX = shrouded pin header, 8 pins [form="♂ (shrouded male)"]
  Part23 = TE_Con_316370-6_040_II SRS_MK-II_48Pin_CAP-ASSY [part_number=316370-6 package="48-pin 0.040\" 3 row"]
  J5 = Screw terminal - 2 pins [package=THT]

nets:
  INJ-1-OUT: J4.pin1, J4.pin40, Part23.2X
  INJ-2-OUT: J4.pin2, J4.pin39, Part23.2W
  INJ-3-OUT: J4.pin3, J4.pin4, Part23.2V
  INJ-4-OUT: J4.pin5, J4.pin6, Part23.2S
  IGN-1-OUT: J4.pin7, Part23.2L
  IGN-4-OUT: J4.pin8, Part23.2O
  GND: J4.pin9, J4.pin10, J4.pin12, J4.pin23, AUX.pin7, AUX.pin8, Part23.2A, Part23.2D, Part23.2E, Part23.2G, Part23.2H, J5.pin2
  MAP-CPU-A3: J4.pin11, Part23.2J
  5V: J4.pin13, J4.pin28, Part23.1E, Part23.1F, Part23.1H, Part23.1I
  ETH-ICD14: J4.pin14, Part23.1X
  Fan-IDC15: J4.pin15, Part23.1V
  FuelPump-IDC16: J4.pin16, Part23.1W
  TacH-IDC17: J4.pin17, Part23.1S
  Clutch-IDC18: J4.pin18, Part23.1T
  CLT Sensor: J4.pin19, Part23.1P
  IAT Sensor: J4.pin20, Part23.1Q
  O2 Sensor: J4.pin21, Part23.1U
  TPS Sensor: J4.pin22, Part23.1R
  VR2+: J4.pin24, Part23.1O
  VR1+: J4.pin25, Part23.1N
  VR2-: J4.pin26, Part23.1L
  VR1-: J4.pin27, Part23.1M
  STEP-2B-OUT: J4.pin29, Part23.2C
  STEP-2A-OUT: J4.pin30, Part23.2F
  STEP-1A-OUT: J4.pin31, Part23.2I
  STEP-1B-OUT: J4.pin32, Part23.2K
  IGN-3-OUT: J4.pin33, Part23.2M
  IGN-2-OUT: J4.pin34, Part23.2N
  BOOST-OUT: J4.pin35, Part23.2Q
  HC-1-OUT: J4.pin36, Part23.2R
  IDLE-OUT: J4.pin37, Part23.2U
  HC-2-OUT: J4.pin38, Part23.2P
  D43: AUX.pin1, Part23.1J
  D53: AUX.pin2, Part23.1G
  D46: AUX.pin3, Part23.1D
  D48: AUX.pin4, Part23.1A
  A7: AUX.pin5, Part23.1B
  A5: AUX.pin6, Part23.1C
  12V-raw: Part23.2B, J5.pin1

notes:
  inj1
  Aaron S. 2020
  [ 0-5v Spare Input ]
  D43
  [ Spare Outputs ]
  D53
  D46
  D48
  A5 A7
  GND GND

custom parts:
  TE_Con_316370-6_040_II SRS_MK-II_48Pin_CAP-ASSY: TE Connectors_316370-6_040_II SRS_MK-II_48Pin_CAP-ASSY
