# Fritzing sketch v0.1.3 (saved by Fritzing 0.9.4)
circuit board: 10cm x 5cm

parts:
  J4 = shrouded pin header, 40 pins [form="♂ (shrouded male)"]
  AUX = shrouded pin header, 8 pins [form="♂ (shrouded male)"]
  Part23 = TE_Con_316370-6_040_II SRS_MK-II_48Pin_CAP-ASSY [part_number=316370-6 package="48-pin 0.040\" 3 row"]
  12v_GND = screw terminal, 2 pins

nets (from the pcb view):
  N1: J4.pin1, J4.pin40, Part23.2X
  N2: J4.pin2, J4.pin39, Part23.2W
  N3: J4.pin3, J4.pin4, Part23.2V
  N4: J4.pin5, J4.pin6, Part23.2S
  N5: J4.pin7, Part23.2L
  N6: J4.pin8, Part23.2O
  N7: J4.pin11, Part23.2J
  N8: J4.pin13, J4.pin28, Part23.1E, Part23.1F, Part23.1H, Part23.1I
  N9: J4.pin14, Part23.1X
  N10: J4.pin15, Part23.1V
  N11: J4.pin16, Part23.1W
  N12: J4.pin17, Part23.1S
  N13: J4.pin18, Part23.1T
  N14: J4.pin19, Part23.1P
  N15: J4.pin20, Part23.1Q
  N16: J4.pin21, Part23.1U
  N17: J4.pin22, Part23.1R
  N18: J4.pin24, Part23.1O
  N19: J4.pin25, Part23.1N
  N20: J4.pin26, Part23.1L
  N21: J4.pin27, Part23.1M
  N22: J4.pin29, Part23.2C
  N23: J4.pin30, Part23.2F
  N24: J4.pin31, Part23.2I
  N25: J4.pin32, Part23.2K
  N26: J4.pin33, Part23.2M
  N27: J4.pin34, Part23.2N
  N28: J4.pin35, Part23.2Q
  N29: J4.pin36, Part23.2R
  N30: J4.pin37, Part23.2U
  N31: J4.pin38, Part23.2P
  N32: AUX.pin1, Part23.1J
  N33: AUX.pin2, Part23.1G
  N34: AUX.pin3, Part23.1D
  N35: AUX.pin4, Part23.1A
  N36: AUX.pin5, Part23.1B
  N37: AUX.pin6, Part23.1C
  N38: Part23.2A, Part23.2D, Part23.2E, Part23.2G, Part23.2H
  N39: Part23.2B, 12v_GND.pin2

notes:
  inj1
  Aaron S. 2020
  [ 0-5v Spare Input ]
  D43
  [ Spare Outputs ]
  D53
  D46
  D48
  A5 A7
  GND GND

custom parts:
  TE_Con_316370-6_040_II SRS_MK-II_48Pin_CAP-ASSY: TE Connectors_316370-6_040_II SRS_MK-II_48Pin_CAP-ASSY
