# Fritzing sketch Clutch Pull Up-Down (saved by Fritzing 0.9.4)
breadboards: 1

parts:
  R78 = Resistor [tolerance=±5% resistance=470 package="0805 [SMD]"]
  D59 = Schottky Diode [part_number=1N5818 package="300 mil [THT]"]
  D60 = Schottky Diode [part_number=1N5818 package="300 mil [THT]"]
  J217 = female pin header, 3 pins [form="♀ (female)"]
  R79 = Resistor [tolerance=±5% resistance=2.2k package=THT]

nets:
  Clutch-IDC18: R78.Pin_0, R79.Pin_0
  LC-CPU-D51: R78.Pin_1, D59.cathode, D60.anode
  GND: D59.anode, J217.pin3
  5V: D60.cathode, J217.pin1
  N1: J217.pin2, R79.Pin_1

notes:
  GND     5v
