# Fritzing sketch v1.2.5b (saved by Fritzing 0.9.4)
circuit board: 10cm x 10cm

parts:
  Arduino_Mega_2560 = Arduino Mega 2560 (Rev3) [part_number="Arduino Mega 2560"]
  Q1 = Basic FET N-Channel [part_number=STP62NS04Z package="TO220 [THT]"]
  Q2 = Basic FET N-Channel [part_number=STP62NS04Z package="TO220 [THT]"]
  Q3 = Basic FET N-Channel [part_number=STP62NS04Z package="TO220 [THT]"]
  Q4 = Basic FET N-Channel [part_number=STP62NS04Z package="TO220 [THT]"]
  U1 = Voltage Regulator - 5V [part_number=LM2940T-5.0 package="TO220 [THT]"]
  U2 = V18ZA2P [part_number=ERZV14D220 package=v18za2p]
  IC3 = IC, DIP package, 8 pins [chip_label="Dual VR Conditioner"]
  JP1 = female pin header, 3 pins [form="♀ (female)"]
  JP2 = female pin header, 3 pins [form="♀ (female)"]
  JP3 = female pin header, 3 pins [form="♀ (female)"]
  JP4 = female pin header, 2 pins [form="♀ (female)"]
  JP5 = female pin header, 2 pins [form="♀ (female)"]
  Q5 = Basic FET N-Channel [part_number=STP62NS04Z package="TO220 [THT]"]
  Q7 = Basic FET N-Channel [part_number=STP62NS04Z package="TO220 [THT]"]
  Q6 = Basic FET N-Channel [part_number=STP62NS04Z package="TO220 [THT]"]
  Q8 = Basic FET N-Channel [part_number=STP62NS04Z package="TO220 [THT]"]
  J63 = female pin header, 1 pin [form="♀ (female)"]
  DRV8825 = Pololu A4988 [package=SO16]
  J124 = female pin header, 1 pin [form="♀ (female)"]
  J143 = female pin header, 1 pin [form="♀ (female)"]  # not connected
  J144 = female pin header, 1 pin [form="♀ (female)"]  # not connected
  C5 = Ceramic Capacitor [capacitance=0.1µF package="0805 [SMD, multilayer]"]
  C20 = Ceramic Capacitor [capacitance=1µF package="0805 [SMD, multilayer]"]
  C12 = Ceramic Capacitor [capacitance=1µF package="0805 [SMD, multilayer]"]
  C4 = Ceramic Capacitor [capacitance=0.22µF package="0805 [SMD, multilayer]"]
  R62 = Resistor [tolerance=±5% resistance=120 package="0805 [SMD]"]
  C2 = Ceramic Capacitor [capacitance=0.22µF package="0805 [SMD, multilayer]"]
  R7 = Resistor [tolerance=±0.1% resistance=3.9k package="0805 [SMD]"]
  R1 = Resistor [tolerance=±0.1% resistance=2.49k package="0805 [SMD]"]
  C8 = Ceramic Capacitor [capacitance=0.22µF package="0805 [SMD, multilayer]"]
  C7 = Ceramic Capacitor [capacitance=0.1µF package="0805 [SMD, multilayer]"]
  R59 = Resistor [tolerance=±5% resistance=220 package="0805 [SMD]"]
  R40 = Resistor [tolerance=±5% resistance=1k package="0805 [SMD]"]
  R39 = Resistor [tolerance=±5% resistance=1k package="0805 [SMD]"]
  R60 = Resistor [tolerance=±5% resistance=1k package="0805 [SMD]"]
  C24 = Ceramic Capacitor [capacitance=100nF package="0805 [SMD, multilayer]"]
  R3 = Resistor [tolerance=±0.1% resistance=2.49k package="0805 [SMD]"]
  C10 = Ceramic Capacitor [capacitance=0.22µF package="0805 [SMD, multilayer]"]
  C9 = Ceramic Capacitor [capacitance=0.1µF package="0805 [SMD, multilayer]"]
  C25 = Ceramic Capacitor [capacitance=0.01µF package="0805 [SMD, multilayer]"]
  C3 = Ceramic Capacitor [capacitance=0.1µF package="0805 [SMD, multilayer]"]
  R2 = Resistor [tolerance=±5% resistance=470 package="0805 [SMD]"]
  R4 = Resistor [tolerance=±5% resistance=470 package="0805 [SMD]"]
  R22 = Resistor [tolerance=±5% resistance=470 package="0805 [SMD]"]
  R6 = Resistor [tolerance=±5% resistance=470 package="0805 [SMD]"]
  C6 = Ceramic Capacitor [capacitance=0.22µF package="0805 [SMD, multilayer]"]
  R31 = Resistor [tolerance=±5% resistance=10 power=1 package="0805 [SMD]"]
  R32 = Resistor [tolerance=±5% resistance=10 power=2W package="0805 [SMD]"]
  R8 = Resistor [tolerance=±5% resistance=470 package="0805 [SMD]"]
  R21 = Resistor [tolerance=±5% resistance=1k package="0805 [SMD]"]
  R49 = Resistor [tolerance=±5% resistance=100k power=0.25W package="0805 [SMD]"]
  R55 = Resistor [tolerance=±5% resistance=100k package="0805 [SMD]"]
  R48 = Resistor [tolerance=±5% resistance=100k package="0805 [SMD]"]
  R56 = Resistor [tolerance=±5% resistance=100k power=0.25W package="0805 [SMD]"]
  R51 = Resistor [tolerance=±5% resistance=1k package="0805 [SMD]"]
  R57 = Resistor [tolerance=±5% resistance=1k package="0805 [SMD]"]
  R50 = Resistor [tolerance=±5% resistance=1k package="0805 [SMD]"]
  R58 = Resistor [tolerance=±5% resistance=1k package="0805 [SMD]"]
  R27 = Resistor [tolerance=±5% resistance=10 power=2W package="0805 [SMD]"]
  R25 = Resistor [tolerance=±5% resistance=10 power=2W package="0805 [SMD]"]
  R35 = Resistor [tolerance=±5% resistance=100k package="0805 [SMD]"]
  R37 = Resistor [tolerance=±5% resistance=100k package="0805 [SMD]"]
  R23 = Resistor [tolerance=±5% resistance=1k package="0805 [SMD]"]
  R24 = Resistor [tolerance=±5% resistance=1k package="0805 [SMD]"]
  C11 = Ceramic Capacitor [capacitance=1µF package="0805 [SMD, multilayer]"]
  R38 = Resistor [tolerance=±5% resistance=100k package="0805 [SMD]"]
  R29 = Resistor [tolerance=±5% resistance=1k package="0805 [SMD]"]
  R30 = Resistor [tolerance=±5% resistance=1k package="0805 [SMD]"]
  R36 = Resistor [tolerance=±5% resistance=100k package="0805 [SMD]"]
  R9 = Resistor [tolerance=±5% resistance=100k package="0805 [SMD]"]
  R12 = Resistor [tolerance=±5% resistance=1k power=0.25W package="0805 [SMD]"]
  R10 = Resistor [tolerance=±5% resistance=100k power=0.25W package="0805 [SMD]"]
  R11 = Resistor [tolerance=±5% resistance=1k package="0805 [SMD]"]
  R13 = Resistor [tolerance=±5% resistance=100k package="0805 [SMD]"]
  R15 = Resistor [tolerance=±5% resistance=1k package="0805 [SMD]"]
  R14 = Resistor [tolerance=±5% resistance=100k package="0805 [SMD]"]
  R16 = Resistor [tolerance=±5% resistance=1k package="0805 [SMD]"]
  R41 = Resistor [tolerance=±5% resistance=470 package="0805 [SMD]"]
  C19 = Ceramic Capacitor [capacitance=0.01µF package="0805 [SMD, multilayer]"]
  R61 = Resistor [tolerance=±5% resistance=2.49k package="0805 [SMD]"]
  C15 = Ceramic Capacitor [capacitance=0.1µF voltage=50V package="0805 [SMD, multilayer]"]
  C13 = Ceramic Capacitor [capacitance=0.1µF voltage=50V package="0805 [SMD, multilayer]"]
  J169 = female pin header, 1 pin [form="♀ (female)"]  # not connected
  J170 = female pin header, 1 pin [form="♀ (female)"]  # not connected
  J172 = female pin header, 1 pin [form="♀ (female)"]  # not connected
  J173 = female pin header, 1 pin [form="♀ (female)"]  # not connected
  J174 = female pin header, 1 pin [form="♀ (female)"]  # not connected
  J176 = female pin header, 1 pin [form="♀ (female)"]  # not connected
  J177 = female pin header, 1 pin [form="♀ (female)"]  # not connected
  J180 = female pin header, 1 pin [form="♀ (female)"]  # not connected
  J182 = female pin header, 1 pin [form="♀ (female)"]  # not connected
  J183 = female pin header, 1 pin [form="♀ (female)"]
  J186 = female pin header, 1 pin [form="♀ (female)"]  # not connected
  D16 = Schottky Diode [part_number=1N5919BG package="300 mil [THT]"]
  HC-05 = Bluetooth HC-05 Macho
  IC6 = ULN2003A [package="SO16 [SMD]"]
  R63 = Resistor [tolerance=±5% resistance=10k package="0805 [SMD]"]
  C18 = Ceramic Capacitor [capacitance=10pF package="0805 [SMD, multilayer]"]
  C16 = Tantalum Capacitor [capacitance=10µF voltage=35V package="A 3216 [SMD, tantalum]"]
  C14 = Tantalum Capacitor [capacitance=47µF voltage=10V package="200 mil [THT, tantalum]"]
  R66 = Resistor [tolerance=±5% resistance=2.2 power=2W package="0805 [SMD]"]
  LED1 = smd LED [color="Red (633nm)" package="0805 [SMD]"]
  R67 = Resistor [tolerance=±5% resistance=2.2 power=2W package="0805 [SMD]"]
  LED2 = smd LED [color="Red (633nm)" package="0805 [SMD]"]
  R68 = Resistor [tolerance=±5% resistance=2.2 power=2W package="0805 [SMD]"]
  LED3 = smd LED [color="Red (633nm)" package="0805 [SMD]"]
  R69 = Resistor [tolerance=±5% resistance=2.2 power=2W package="0805 [SMD]"]
  LED4 = smd LED [color="Red (633nm)" package="0805 [SMD]"]
  J4 = shrouded pin header, 40 pins [form="♂ (shrouded male)"]
  C30 = Ceramic Capacitor [capacitance=0.22µF package="0805 [SMD, multilayer]"]
  R65 = Resistor [tolerance=±5% resistance=220 package="0805 [SMD]"]
  C29 = Ceramic Capacitor [capacitance="100 nF" package="0805 [SMD, multilayer]"]
  C28 = Ceramic Capacitor [capacitance="100 nF" package="0805 [SMD, multilayer]"]
  C27 = Ceramic Capacitor [capacitance="100 nF" package="0805 [SMD, multilayer]"]
  C26 = Ceramic Capacitor [capacitance="100 nF" package="0805 [SMD, multilayer]"]
  R64 = Resistor [tolerance=±5% resistance=220 package="0805 [SMD]"]
  A5_A7 = female pin header, 2 pins [form="♀ (female)"]
  R70 = Resistor [tolerance=±5% resistance=2.2 power=2W package="0805 [SMD]"]
  LED5 = smd LED [color="Red (633nm)" package="0805 [SMD]"]
  R71 = Resistor [tolerance=±5% resistance=2.2 power=2W package="0805 [SMD]"]
  LED6 = smd LED [color="Red (633nm)" package="0805 [SMD]"]
  R72 = Resistor [tolerance=±5% resistance=2.2 power=2W package="0805 [SMD]"]
  LED7 = smd LED [color="Red (633nm)" package="0805 [SMD]"]
  R73 = Resistor [tolerance=±5% resistance=2.2 power=2W package="0805 [SMD]"]
  LED8 = smd LED [color="Red (633nm)" package="0805 [SMD]"]
  D17 = Diode [package=sma-diode]
  D18 = Diode [package=sma-diode]
  D19 = Diode [package=sma-diode]
  D20 = Diode [package=sma-diode]
  J3 = screw terminal, 2 pins
  IC4 = SO16 [chip_label=SP720 package=SO]
  IC1 = SO08-EIAJ [chip_label=IC package=SO]
  IC2 = SO08-EIAJ [chip_label=IC part_number=" C44150" package=SO]
  J210 = female pin header, 1 pin [form="♀ (female)"]  # not connected
  J211 = female pin header, 1 pin [form="♀ (female)"]  # not connected
  J212 = female pin header, 1 pin [form="♀ (female)"]
  J213 = female pin header, 1 pin [form="♀ (female)"]  # not connected
  J215 = female pin header, 1 pin [form="♀ (female)"]  # not connected
  C1 = Ceramic Capacitor [capacitance=0.1µF package="0805 [SMD, multilayer]"]
  J110 = female pin header, 4 pins [form="♀ (female)"]
  J109 = female pin header, 4 pins [form="♀ (female)"]
  MPX4250AP1 = MPX4250AP pressure sensor [part_number=MPX]
  JP7 = female pin header, 2 pins [form="♀ (female)"]
  D54 = Diode [package=sma-diode]
  JP6 = female pin header, 2 pins [form="♀ (female)"]
  IC5 = SO08w [chip_label=IC package=SO(w)]
  D15 = Diode [part_number=SS54 package=sma-diode]
  D56 = Zener Diode [part_number=1N4732A breakdown_voltage=3.6V package="300 mil [THT]"]  # not connected
  R75 = Resistor [tolerance=±5% resistance=1k package="0805 [SMD]"]  # not connected

nets (from the pcb view):
  N1: Arduino_Mega_2560.A8, C10.1, R22.Pin_1, IC4.15
  N2: Arduino_Mega_2560.A0, C2.1, R2.Pin_1, IC4.1
  N3: Arduino_Mega_2560.A1, C4.1, R4.Pin_1, IC4.2
  N4: Arduino_Mega_2560.A2, R6.Pin_1, C6.1, IC4.3
  N5: Arduino_Mega_2560.A3, R41.Pin_1, C18.0, J4.pin11, IC4.4
  N6: Arduino_Mega_2560.A4, C8.0, R8.Pin_1, IC4.6
  N7: Arduino_Mega_2560.A5, C27.1, R64.Pin_1, IC4.5
  N8: Arduino_Mega_2560.A7, R65.Pin_1, C29.1, IC4.7
  N9: Arduino_Mega_2560.D19/RX1, IC3.pin8, R59.Pin_1, C25.1, IC4.11
  N10: Arduino_Mega_2560.D18/TX1, IC3.pin7, R60.Pin_1, C24.0, IC4.9
  N11: Arduino_Mega_2560.D17_PWM/RX2, DRV8825.STEP
  N12: Arduino_Mega_2560.D16_PWM/TX2, DRV8825.DIR
  N13: Arduino_Mega_2560.D11_PWM, R14.Pin_0, R16.Pin_0
  N14: Arduino_Mega_2560.D10_PWM, R13.Pin_0, R15.Pin_0
  N15: Arduino_Mega_2560.D9_PWM, R12.Pin_0, R10.Pin_0
  N16: Arduino_Mega_2560.D8_PWM, R9.Pin_0, R11.Pin_0
  N17: Arduino_Mega_2560.RESET, R62.Pin_0
  5V: Arduino_Mega_2560.5V, U1.output_voltage, IC3.pin5, JP1.pin1, DRV8825.RESET, DRV8825.SLEEP, C20.1, R1.Pin_0, R40.Pin_0, R39.Pin_0, R3.Pin_0, C19.1, R61.Pin_1, C13.1, D16.cathode, HC-05.VCC, C14.+, J4.pin13, J4.pin28, IC4.16, J109.pin1, J109.pin2, J109.pin3, J109.pin4, MPX4250AP1.Vs, JP6.pin1, IC5.2
  N18: Arduino_Mega_2560.D0_RX0, JP7.pin1, D54.A
  N19: Arduino_Mega_2560.D1_TX0, HC-05.RXD
  N20: Arduino_Mega_2560.D2_PWM, R61.Pin_0, J4.pin14, C30.1
  N21: Arduino_Mega_2560.D4_PWM, R58.Pin_0
  N22: Arduino_Mega_2560.D5_PWM, R50.Pin_0
  N23: Arduino_Mega_2560.D6_PWM, R57.Pin_0
  N24: Arduino_Mega_2560.D7_PWM, R51.Pin_0
  N25: Arduino_Mega_2560.D24, DRV8825.ENABLE
  N26: Arduino_Mega_2560.D38, R24.Pin_0
  N27: Arduino_Mega_2560.D40, R23.Pin_0
  N28: Arduino_Mega_2560.D43, IC6.In_2
  N29: Arduino_Mega_2560.D45, IC6.In_4
  N30: Arduino_Mega_2560.D46, IC6.In_6
  N31: Arduino_Mega_2560.D47, IC6.In_1
  N32: Arduino_Mega_2560.D48, IC6.In_7
  N33: Arduino_Mega_2560.D49, IC6.In_3
  N34: Arduino_Mega_2560.D50, R30.Pin_0
  N35: Arduino_Mega_2560.D51, J4.pin18
  N36: Arduino_Mega_2560.D52, R29.Pin_0
  N37: Arduino_Mega_2560.D53, IC6.In_5
  N38: Q1.gate, R11.Pin_1
  N39: Q1.drain, J4.pin1, J4.pin40, D17.C
  N40: Q2.gate, R15.Pin_1
  N41: Q2.drain, J4.pin3, J4.pin4, D19.C
  N42: Q3.gate, R12.Pin_1
  N43: Q3.drain, J4.pin2, J4.pin39, D18.C
  N44: Q4.gate, R16.Pin_1
  N45: Q4.drain, J4.pin5, J4.pin6, D20.C
  N46: U1.input_voltage, D15.C
  N47: U2.P$1, JP1.pin3, DRV8825.VMOT, R7.Pin_0, C15.1, IC6.COM_-_Common, R63.Pin_1, C16.+, R70.Pin_0, R71.Pin_0, R72.Pin_0, R73.Pin_0, J3.pin2, D15.A
  N48: IC3.pin1, J4.pin27
  N49: IC3.pin2, JP2.pin3
  N50: IC3.pin3, JP3.pin1
  N51: IC3.pin4, J4.pin26
  N52: JP1.pin2, C12.1, C11.1, IC1.6, IC2.6
  N53: JP2.pin1, R59.Pin_0
  N54: JP2.pin2, JP4.pin2, J4.pin25
  N55: JP3.pin2, JP5.pin1, J4.pin24
  N56: JP3.pin3, R60.Pin_0
  N57: JP4.pin1, R39.Pin_1
  N58: JP5.pin2, R40.Pin_1
  N59: Q5.gate, R55.Pin_1, R57.Pin_1
  N60: Q5.drain, J4.pin36
  N61: Q7.gate, R48.Pin_1, R50.Pin_1
  N62: Q7.drain, J4.pin37
  N63: Q6.gate, R56.Pin_1, R58.Pin_1
  N64: Q6.drain, J4.pin38
  N65: Q8.gate, R49.Pin_1, R51.Pin_1
  N66: Q8.drain, J4.pin35
  N67: J63.pin1, IC6.Out_5
  N68: DRV8825.1B, J4.pin32
  N69: DRV8825.1A, J4.pin31
  N70: DRV8825.2A, J4.pin30
  N71: DRV8825.2B, J4.pin29
  N72: J124.pin1, IC6.Out_7
  N73: C5.1, R6.Pin_0, J4.pin22
  N74: R62.Pin_1, JP6.pin2
  N75: R7.Pin_1, C7.1, R8.Pin_0, R21.Pin_0
  N76: R1.Pin_1, R2.Pin_0, J4.pin20, C1.1
  N77: R3.Pin_1, C3.1, R4.Pin_0, J4.pin19
  N78: C9.1, R22.Pin_0, J4.pin21
  N79: R31.Pin_0, R69.Pin_1, J4.pin33
  N80: R31.Pin_1, IC2.7
  N81: R32.Pin_0, IC2.5
  N82: R32.Pin_1, R68.Pin_1, J4.pin8
  N83: R27.Pin_0, R67.Pin_1, J4.pin7
  N84: R27.Pin_1, IC1.7
  N85: R25.Pin_0, IC1.5
  N86: R25.Pin_1, R66.Pin_1, J4.pin34
  N87: R35.Pin_1, R24.Pin_1, IC1.4
  N88: R37.Pin_1, R23.Pin_1, IC1.2
  N89: R38.Pin_1, R29.Pin_1, IC2.2
  N90: R30.Pin_1, R36.Pin_1, IC2.4
  N91: R41.Pin_0, MPX4250AP1.V_out, IC5.4
  N92: J183.pin1, IC6.Out_6
  N93: HC-05.TXD, JP7.pin2, D54.C
  N94: IC6.Out_4, J4.pin16
  N95: IC6.Out_3, R63.Pin_0, J4.pin17
  N96: IC6.Out_2, J212.pin1
  N97: IC6.Out_1, J4.pin15
  N98: R66.Pin_0, LED1.anode
  N99: R67.Pin_0, LED2.anode
  N100: R68.Pin_0, LED3.anode
  N101: R69.Pin_0, LED4.anode
  N102: J4.pin9, J4.pin10, J4.pin12
  N103: R65.Pin_0, C28.1, A5_A7.pin1
  N104: C26.1, R64.Pin_0, A5_A7.pin2
  N105: R70.Pin_1, LED5.anode
  N106: LED5.cathode, D17.A
  N107: R71.Pin_1, LED6.anode
  N108: LED6.cathode, D18.A
  N109: R72.Pin_1, LED7.anode
  N110: LED7.cathode, D19.A
  N111: R73.Pin_1, LED8.anode
  N112: LED8.cathode, D20.A
  N113: IC1.3, IC2.3
  N114: J110.pin1, J110.pin2, J110.pin3, J110.pin4

notes:
  Injector 1
  Injector 3
  Injector 2
  Injector 4
  Ignitor output 1
  12v
  5v
  Power supply
  IGN Out
  DetonationEMS.com
  Generic Outputs - High Current
  inj1
  VR
  Hall
  Reset Protection - Refer AVR040 Application note
  Stepper Driver
  PWM Idle / Boost
  GND
  Proto Area
  Remove to Prog
  v1.2b
  Aaron S. 2020
  Protection
  TX RX
  GND VCC
  Flex Input
  TPS Input
  o2 Input
  IAT Input
  Battery Ref
  Coolant Temp
  A5,A7 0-5v Spare Input
  Select Board Layout "Speeduino V0.4"
  D53
  D43
  | Spare Outputs |
  D46
  D48
  Flat side down
  THT Map Sensor
  1
  4
  5
  8

custom parts:
  Diode: Diode These are standard reverse protection diodes and small signal diodes. SMA package can handle up to about 1A. SOD-323 can handle about 200mA. What the SOD-323 package when ordering, there are some mfgs out there that are 5-pin packages.
